# Fritzing sketch Firefighter Robot (saved by Fritzing 0.9.6b)
circuit board: 17.2214cm x 9.07466cm

parts:
  Part1 = Arduino Uno (Rev3) - ICSP
  J1 = Basic Servo
  S1 = H-Bridge with L298N
  Part2 = Bluetooth HC-05 Macho
  M1 = DC Motor
  M2 = DC Motor
  SG1 = Buzzer 12mm [package=buzzer-ccv-kit]
  WATER_PUMP1 = water pump/motor
  Mod1 = KY-026 Flame Sensor Module [package="Breakout board"]
  Mod2 = KY-026 Flame Sensor Module [package="Breakout board"]
  Mod3 = KY-026 Flame Sensor Module [package="Breakout board"]
  M4 = DC Motor
  M3 = DC Motor
  U2 = LIPO-2000mAh [package=lipo-2000]  # not connected
  Q1 = NPN-Transistor [package="SOT-23 [SMD]"]

nets (from the pcb view):
  N1: Part1.A0, Mod3.D0
  N2: Part1.A1, Mod2.D0
  N3: Part1.A2, Mod1.D0
  VCC: Part1.5V, J1.vcc, Part2.VCC, Mod1.+, Mod2.+, Mod3.+
  N4: Part1.D8, S1.IN1
  N5: Part1.D9_PWM, S1.IN2
  N6: Part1.D10_PWM/SS, S1.IN3
  N7: Part1.D11_PWM/MOSI, S1.IN4
  N8: Part1.D12/MISO, S1.ENB
  N9: Part1.D13/SCK, SG1.1
  GND: Part1.GND, J1.gnd, S1.GND, Part2.GND, SG1.2, Mod1.G, Mod2.G, Mod3.G, Q1.1
  N10: Part1.D0/RX, Part2.TXD
  N11: Part1.D1/TX, Part2.RXD
  N12: Part1.D4, Part1.D6_PWM, J1.pulse
  N13: Part1.D5_PWM, Q1.0
  N14: Part1.D7, S1.ENA
  VIN: Part1.VIN, S1.5V
  N15: S1.M1-01, M1.pin_2, M2.pin_2
  N16: S1.M1-02, M1.pin_1, M2.pin_1
  N17: S1.M2-01, M4.pin_1, M3.pin_1
  N18: S1.M2-02, M4.pin_2, M3.pin_2
  N19: WATER_PUMP1.pin_2, Q1.2

custom parts:
  H-Bridge with L298N: h-bridge
  water pump/motor: WATER PUMP BY ARDUBLOCKTR
  KY-026 Flame Sensor Module: KY-026 Flame Sensor Module reacts in the presence of fire.

// code stored in the sketch: Untitled2.ino
#include "Servo.h"

#define RightFlame A0
#define MiddleFlame  A1
#define LeftFlame  A2

#define Pump 3

#define ServoPIN 4

#define RMSpeed 6
#define RM1 8
#define RM2 7
#define LM1 10
#define LM2 9
#define LMSpeed 11

#define Buzzer 5

void CarControl(char command);
void SetMotorSpeed(char command);
void ServoControl(char command);
void PumpControl(char command);
void SetPumpSpeed(char command);
void SetMode(char command);
void ExtinguishFire(int dir);
int DetectFire(int sensor);
void CarStop();

Servo MyServo; 

int ServoPosition = 90;
int MotorSpeed = 140;
int PumpSpeed = 170;

bool ManualMode = false;
bool AutoMode = false;

void setup() {
  Serial.begin(9600);

  MyServo.attach(ServoPIN);
  
  pinMode(RightFlame, INPUT);
  pinMode(MiddleFlame, INPUT);
  pinMode(LeftFlame, INPUT);

  pinMode(RM1, OUTPUT);
  pinMode(RM2, OUTPUT);
  pinMode(LM1, OUTPUT);
  pinMode(LM2, OUTPUT);
  pinMode(Pump, OUTPUT);
  pinMode(Buzzer, OUTPUT);

  analogWrite(RMSpeed, MotorSpeed);
  analogWrite(LMSpeed, MotorSpeed);

  analogWrite(Pump, PumpSpeed);

  MyServo.write(ServoPosition);
  CarStop();
  digitalWrite(Pump, LOW);
  digitalWrite(Buzzer, LOW);
}




void loop() {
  if(Serial.available()){
    char input = Serial.read();
    SetMode(input);
    if(input == 'A'){
      Serial.print("Automatic Mode On!\n");
    }else if(input == 'M'){
      Serial.print("Manual Mode Off!\n");
    }
    
    while(AutoMode){
      if(Serial.available()){
        input = Serial.read();
        SetMode(input);
      }
      CarStop();
      
      if(DetectFire(RightFlame) || DetectFire(MiddleFlame) || DetectFire(LeftFlame)) {
        digitalWrite(Buzzer, HIGH);
        if(DetectFire(RightFlame)){
          ExtinguishFire(45);
        } else if(DetectFire(MiddleFlame)){
          ExtinguishFire(90);
        } else if(DetectFire(LeftFlame)){
          ExtinguishFire(135);
        }
        digitalWrite(Buzzer, LOW);
      }
    }

    while(ManualMode){
      if(Serial.available()){
        input = Serial.read();
        SetMode(input);
        CarControl(input);
        SetMotorSpeed(input);
        ServoControl(input);
        PumpControl(input);
        SetPumpSpeed(input);
        CarStop();
      }
    }
  }
}

void CarControl(char command) {
  switch (command) {
    case 'F': // Forward
      digitalWrite(RM1, HIGH);
      digitalWrite(RM2, LOW);
      digitalWrite(LM1, HIGH);
      digitalWrite(LM2, LOW);
      delay(20);
      break;
      
    case 'B': // Backward
      digitalWrite(RM1, LOW);
      digitalWrite(RM2, HIGH);
      digitalWrite(LM1, LOW);
      digitalWrite(LM2, HIGH);
      delay(20);
      break;

    case 'R': // Turn Right
      digitalWrite(RM1, LOW);
      digitalWrite(RM2, LOW);
      digitalWrite(LM1, HIGH);
      digitalWrite(LM2, LOW);
      delay(40);
      break;

    case 'L': // Turn Left
      digitalWrite(RM1, HIGH);
      digitalWrite(RM2, LOW);
      digitalWrite(LM1, LOW);
      digitalWrite(LM2, LOW);
      delay(40);
      break;

  }
}

void SetMotorSpeed(char command){
  if(command == 'P'){
    MotorSpeed += 10;
    if(MotorSpeed > 180) MotorSpeed = 1808;
    analogWrite(RMSpeed, MotorSpeed);
    analogWrite(LMSpeed, MotorSpeed);
    Serial.print("Motor Speed: ");
    Serial.println(MotorSpeed);
  }else if(command == 'N'){
    MotorSpeed -= 10;
    if(MotorSpeed < 80) MotorSpeed = 80;
    analogWrite(RMSpeed, MotorSpeed);
    analogWrite(LMSpeed, MotorSpeed);
    Serial.print("Motor Speed: ");
    Serial.println(MotorSpeed);
  }
  
}

void ServoControl(char command){
  if(command == '-'){
    ServoPosition+=10;
    if(ServoPosition > 135) ServoPosition = 135;
    MyServo.write(ServoPosition);
    delay(5);

  }else if(command == '+'){
    ServoPosition-=10;
    if(ServoPosition < 45) ServoPosition = 45;
    MyServo.write(ServoPosition--);
    delay(5);
  }
}



void PumpControl(char command){
  if(command == 'W'){
    digitalWrite(Buzzer, HIGH);
    digitalWrite(Pump, HIGH);
    Serial.print("Pump On");
  }else if(command == 'V'){
    digitalWrite(Buzzer, LOW);
    digitalWrite(Pump, LOW);
    Serial.print("Pump Off");
  }
}

void SetPumpSpeed(char command){
  if(command == 'Z'){
    PumpSpeed += 10;
    if(PumpSpeed > 255) PumpSpeed = 255;
    analogWrite(Pump, PumpSpeed);
    Serial.print("Pump Speed: ");
    Serial.println(PumpSpeed);
    
  }else if(command == 'X'){
    MotorSpeed -= 10;
    if(PumpSpeed < 130) PumpSpeed = 130;
    analogWrite(Pump, PumpSpeed);
    Serial.print("Pump Speed: ");
    Serial.println(PumpSpeed);
  }
}

void SetMode(char command){
  if(command == 'A'){
    AutoMode = true;
    ManualMode = false;
    Serial.print("Set Automatic\n");
  }else if(command == 'M'){
    AutoMode = false;
    ManualMode = true;
    Serial.print("Set Manual\n");
  }
}

void ExtinguishFire(int dir) {
  MyServo.write(dir);
  delay(500);
  digitalWrite(Pump, HIGH);
  delay(500);
  while (DetectFire(RightFlame) || DetectFire(MiddleFlame) || DetectFire(LeftFlame)) {
    delay(100);
    Serial.print("Fire!\n");
  }

  digitalWrite(Pump, LOW);
}

int DetectFire(int sensor) {
  return !digitalRead(sensor);
}


void CarStop(){
  digitalWrite(RM1, LOW);
  digitalWrite(RM2, LOW);
  digitalWrite(LM1, LOW);
  digitalWrite(LM2, LOW);
}
